# Fritzing sketch schematic (saved by Fritzing 0.8.7b)

parts:
  M1 = MT3608 Module
  L298N1 = L298N DC motor driver
  IC1 = KS0029 [chip_label=?]
  U2 = SWITCH_SPDT [package=kps-1290]
  M2 = DC Motor  # not connected
  BAT6 = 18650 battery holder [package=battery-18650-kit]
  M3 = DC Motor  # not connected
  JP6 = Header 12 [package=1x12_machine-pin-header_lock.004]
  Mod1 = Raspberry Pi Pico
  Εξάρτημα1 = Adafruit TCS34725 RGB Color Sensor [part_number="Adafruit #1334"]
  JP7 = Header 12 [package=1x12_machine-pin-header_lock.004]
  J1 = Basic Servo

nets:
  N1: M1.pin1, BAT6.+
  N2: M1.pin2, U2.S
  N3: M1.pin3, JP7.11, JP7.12
  N4: M1.pin4, L298N1.GND, JP6.1, JP6.5, JP6.8, JP6.12
  N5: L298N1.12V, JP7.3
  N6: L298N1.5V#9, L298N1.ENA
  N7: L298N1.5V#10, L298N1.ENB
  N8: L298N1.IN1, Mod1.pin_2
  N9: L298N1.IN2, Mod1.pin_4
  N10: L298N1.IN3, Mod1.pin_5
  N11: L298N1.IN4, Mod1.pin_6
  N12: IC1.GND, JP6.10
  VCC: IC1.VCC, Mod1.pin_40, JP7.1, JP7.6, JP7.9, J1.vcc
  N13: IC1.S, Mod1.pin_1
  N14: U2.P, BAT6.-
  N15: JP6.7, Mod1.pin_33, Mod1.pin_38, Εξάρτημα1.GND
  N16: Mod1.pin_12, J1.pulse
  N17: Mod1.pin_31, Εξάρτημα1.SDA
  N18: Mod1.pin_32, Εξάρτημα1.SCL
  N19: Mod1.pin_36, Εξάρτημα1.+3V3

custom parts:
  MT3608 Module: MT3608 Boost Converter Module Links: Aerosemi MT3608 2A Step Up Converter datasheet
  L298N DC motor driver: 2x DC motor driver with 78M05 positive voltage regulator (7..35 V) L298N: max 46 V, 2 A Set 5 V Enable jumper to enable 5 V regultor (needed for the L298N) and +5 V output at screw terminal or supply external +5 V at screw terminal Set ENA and/or ENB to +5 V to enable motor permanently or supply ENA and/or ENB with PWM signal IN1 and IN2 set rotation directory for motor A (OUT1/OUT2) IN2 and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
  KS0029: Button
  18650 battery holder: 18650 Battery
  Raspberry Pi Pico: Raspberry Pi Pico. Based around the RP2040 microcontroller the Pico is a low cost microcontroller device bringing Raspberry Pi quality, cost, and easy of use to the microcontroller space. Jan 2021, Split part in to two versions: tht (this one) and SMD. This one will drill holes for a .1 in header in pcb to allow plugging in the module as well as providing pads to solder the module to the top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
  Adafruit TCS34725 RGB Color Sensor: Your electronics can now see in dazzling color with this lovely color light sensor. We found the best color sensor on the market, the TCS34725, which has RGB and Clear light sensing elements. An IR blocking filter, integrated on-chip and localized to the color sensing photodiodes, minimizes the IR spectral component of the incoming light and allows color measurements to be made accurately. The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
